// Logisim project trab3.circ as structural Verilog: 2 circuits, main circuit memoria
module memoria (
);

  wire [7:0] multiplexer_2_out;
  wire [15:0] multiplexer_1_out, ram_1_dout, ram_3_dout;

  RAM #(.addrWidth(24), .databus("bibus")) ram_1 (.dout(ram_1_dout[7:0]));  // open: addr, we, oe, clk, din
  RAM #(.addrWidth(24), .databus("bibus")) ram_2 (.dout(ram_1_dout[15:8]));  // open: addr, we, oe, clk, din
  RAM #(.addrWidth(24), .databus("bibus")) ram_3 (.dout(ram_3_dout[7:0]));  // open: addr, we, oe, clk, din
  RAM #(.addrWidth(24), .databus("bibus")) ram_4 (.dout(ram_3_dout[15:8]));  // open: addr, we, oe, clk, din
  Multiplexer #(.width(16), .enable("false")) multiplexer_1 (
    .in0(ram_1_dout), .in1(ram_3_dout), .out(multiplexer_1_out));  // open: sel
  Multiplexer #(.select(2), .width(8), .enable("false")) multiplexer_2 (
    .in0(ram_1_dout[7:0]), .in1(ram_1_dout[15:8]), .in2(ram_3_dout[7:0]), .in3(ram_3_dout[15:8]),
    .out(multiplexer_2_out));  // open: sel
  Multiplexer #(.select(2), .width(32), .enable("false")) multiplexer_3 (
    .in0({ram_3_dout, ram_1_dout}), .in1({{16{1'b0}}, multiplexer_1_out}),
    .in2({{24{1'b0}}, multiplexer_2_out}));  // open: in3, out, sel
endmodule

module singExt (
  input  [15:0] signextIN,
  input  [31:0] signextOUT
);


  assign signextOUT = {{17{signextIN[15]}}, signextIN[14:0]};
endmodule
